# Fritzing sketch lcd_hello_world (saved by Fritzing 0.9.3b)
breadboards: 1

parts:
  LCD1 = LCD screen
  Part1 = Arduino Uno (Rev3) - ICSP
  part = Resistor [tolerance=±5% resistance=220 package=THT]
  U1 = POT [package=pot_mammoth]

nets:
  VSS: LCD1.VSS, LCD1.R/W, LCD1.LED-, Part1.GND, U1.E
  VDD: LCD1.VDD, Part1.5V, part.Pin_0, U1.S
  N1: LCD1.V0, U1.A
  N2: LCD1.RS, Part1.ICSP_MISO, Part1.D12/MISO
  N3: LCD1.E, Part1.D11_PWM/MOSI
  N4: LCD1.DB4, Part1.D5_PWM
  N5: LCD1.DB5, Part1.D4
  N6: LCD1.DB6, Part1.D3_PWM
  N7: LCD1.DB7, Part1.D2
  N8: LCD1.LED+, part.Pin_1

notes:
  D5,4,3,2 - DBG4,5,6,7
  D12,11 - RS, E
  5V
  10k ohm
  GND
  VSS - GND
  VDD - 5V
  Vo - 10k ohm
  RS - D12
  DB4 - D5
  DB5 - D4
  DB6 - D3
  DB7 - D2
